// Logisim project crash_rock.circ as structural Verilog: 4 circuits, main circuit main
module main (
);

  wire and_1_out, ball_1_carry, clock_1_out, j_k_ff_1_q, j_k_ff_2_q, j_k_ff_3_q, keyboard_1_avail, or_1_out,
       PAUSE, pla_1_out, pla_3_out, pla_4_out, pla_7_out, pla_8_out, pla_9_out, RESET, undriven, updown_carry;
  wire [4:0] updown_q;
  wire [6:0] keyboard_1_data, score_1_hundred, score_1_one, score_1_ten;
  wire [19:0] and_2_out, and_3_out, ball_1_o, bar_1_o, bit_extender_1_out, demultiplexer_1_out0,
       demultiplexer_1_out1, demultiplexer_1_out2, demultiplexer_1_out3, demultiplexer_1_out4,
       demultiplexer_1_out5, demultiplexer_1_out6, demultiplexer_1_out7, demultiplexer_1_out8,
       demultiplexer_1_out9, demultiplexer_1_out10, demultiplexer_1_out11, demultiplexer_1_out12,
       demultiplexer_1_out13, demultiplexer_1_out14, demultiplexer_1_out15, demultiplexer_1_out16,
       demultiplexer_1_out17, demultiplexer_1_out18, demultiplexer_1_out19, multiplexer_1_out,
       multiplexer_2_out, pla_2_out, shifter_1_out, shifter_2_out, xnor_1_out;

  Clock clock_1 (.out(clock_1_out));
  J_K_Flip_Flop j_k_ff_1 (.J(1'b1), .K(1'b1), .clk(PAUSE), .Q(j_k_ff_1_q));  // open: Qn, preset, reset
  Counter #(.max('h13), .ongoal("stay"), .width(5)) updown (
    .clr(pla_1_out), .up(j_k_ff_3_q), .count(j_k_ff_1_q), .clk(clock_1_out), .carry(updown_carry),
    .Q(updown_q));  // open: load, D
  J_K_Flip_Flop j_k_ff_2 (
    .J(ball_1_carry), .K(ball_1_carry), .clk(clock_1_out), .Q(j_k_ff_2_q));  // open: Qn, preset, reset
  ball ball_1 (
    .Set(20'h1), .RESET(pla_1_out), .LOAD(1'b0), .Count(j_k_ff_2_q), .EN(j_k_ff_1_q), .CL(clock_1_out),
    .I({5{1'b0}}), .Carry(ball_1_carry), .O(ball_1_o));
  or or_1 (or_1_out, pla_9_out, updown_carry);
  J_K_Flip_Flop j_k_ff_3 (.J(or_1_out), .K(or_1_out), .clk(clock_1_out), .Q(j_k_ff_3_q));  // open: Qn, preset, reset
  and and_1 (and_1_out, ~j_k_ff_3_q, pla_3_out);  // AND_Gate
  PLA #(.in_width(5), .out_width(1), .\table ("10011 1")) pla_1 (.in(updown_q), .out(pla_1_out));
  Demultiplexer #(.select(5), .width(20)) demultiplexer_1 (
    .out0(demultiplexer_1_out0), .out1(demultiplexer_1_out1), .out2(demultiplexer_1_out2),
    .out3(demultiplexer_1_out3), .out4(demultiplexer_1_out4), .out5(demultiplexer_1_out5),
    .out6(demultiplexer_1_out6), .out7(demultiplexer_1_out7), .out8(demultiplexer_1_out8),
    .out9(demultiplexer_1_out9), .out10(demultiplexer_1_out10), .out11(demultiplexer_1_out11),
    .out12(demultiplexer_1_out12), .out13(demultiplexer_1_out13), .out14(demultiplexer_1_out14),
    .out15(demultiplexer_1_out15), .out16(demultiplexer_1_out16), .out17(demultiplexer_1_out17),
    .out18(demultiplexer_1_out18), .out19(demultiplexer_1_out19), .in(ball_1_o), .sel(updown_q));  // open: out20, out21, out22, out23, out24, out25, out26, out27, out28, out29, out30, out31
  PLA #(.in_width(5), .out_width(20), .\table ("10000 11111111111111111111 # 16")) pla_2 (
    .in(updown_q), .out(pla_2_out));
  PLA #(.in_width(5), .out_width(1), .\table ("10000 1")) pla_3 (.in(updown_q), .out(pla_3_out));
  score score_1 (.Reset(RESET), .i(undriven), .ten(score_1_ten), .hundred(score_1_hundred), .one(score_1_one));
  Multiplexer #(.width(20)) multiplexer_1 (
    .in0(bar_1_o), .in1(demultiplexer_1_out18), .out(multiplexer_1_out), .sel(pla_4_out));
  PLA #(.in_width(5), .out_width(1), .\table ("10010 1")) pla_4 (.in(updown_q), .out(pla_4_out));
  DotMatrix #(.inputtype("row"), .matrixcols(20), .matrixrows(20)) dotmatrix_1 (
    .row0(demultiplexer_1_out0), .row1(demultiplexer_1_out1), .row2(demultiplexer_1_out2),
    .row3(demultiplexer_1_out3), .row4(demultiplexer_1_out4), .row5(demultiplexer_1_out5),
    .row6(demultiplexer_1_out6), .row7(demultiplexer_1_out7), .row8(demultiplexer_1_out8),
    .row9(demultiplexer_1_out9), .row10(demultiplexer_1_out10), .row11(demultiplexer_1_out11),
    .row12(demultiplexer_1_out12), .row13(demultiplexer_1_out13), .row14(demultiplexer_1_out14),
    .row15(demultiplexer_1_out15), .row16(demultiplexer_1_out16), .row17(demultiplexer_1_out17),
    .row18(multiplexer_1_out), .row19(demultiplexer_1_out19));
  Keyboard keyboard_1 (.clr(keyboard_1_avail), .avail(keyboard_1_avail), .data(keyboard_1_data));  // open: clk, re
  Shifter #(.shift("lr"), .width(20)) shifter_1 (.in(demultiplexer_1_out16), .\dist (5'b00010), .out(shifter_1_out));
  Shifter #(.width(20)) shifter_2 (.in(demultiplexer_1_out16), .\dist (5'b00010), .out(shifter_2_out));
  PLA #(.in_width(7), .out_width(1), .\table ("1110010 1")) pla_5 (.in(keyboard_1_data), .out(RESET));
  PLA #(.in_width(7), .out_width(1), .\table ("0001010 1")) pla_6 (.in(keyboard_1_data), .out(PAUSE));
  Multiplexer #(.width(20)) multiplexer_2 (
    .in0(shifter_1_out), .in1(shifter_2_out), .out(multiplexer_2_out), .sel(j_k_ff_2_q));
  assign bit_extender_1_out = {{19{j_k_ff_3_q}}, j_k_ff_3_q};  // Bit_Extender bit_extender_1
  PLA #(.in_width(7), .out_width(1), .\table ("1100001 1")) pla_7 (.in(keyboard_1_data), .out(pla_7_out));
  PLA #(.in_width(7), .out_width(1), .\table ("1100100 1")) pla_8 (.in(keyboard_1_data), .out(pla_8_out));
  assign and_2_out = bar_1_o & multiplexer_2_out;  // AND_Gate and_2, 20 bits wide
  _7_Segment_Display u_7_segment_display_1 (
    .g(score_1_hundred[0]), .f(score_1_hundred[1]), .a(score_1_hundred[6]), .b(score_1_hundred[5]),
    .e(score_1_hundred[2]), .d(score_1_hundred[3]), .c(score_1_hundred[4]));  // open: dp
  assign xnor_1_out = ~(and_2_out ^ multiplexer_2_out);  // XNOR_Gate xnor_1, 20 bits wide
  _7_Segment_Display u_7_segment_display_2 (
    .g(score_1_one[0]), .f(score_1_one[1]), .a(score_1_one[6]), .b(score_1_one[5]), .e(score_1_one[2]),
    .d(score_1_one[3]), .c(score_1_one[4]));  // open: dp
  _7_Segment_Display u_7_segment_display_3 (
    .g(score_1_ten[0]), .f(score_1_ten[1]), .a(score_1_ten[6]), .b(score_1_ten[5]), .e(score_1_ten[2]),
    .d(score_1_ten[3]), .c(score_1_ten[4]));  // open: dp
  assign and_3_out = xnor_1_out & bit_extender_1_out & pla_2_out;  // AND_Gate and_3, 20 bits wide
  PLA #(.in_width(20), .out_width(1), .\table ("11111111111111111111 1")) pla_9 (.in(and_3_out), .out(pla_9_out));
  bar bar_1 (.Set(20'h3f), .A(pla_7_out), .D(pla_8_out), .O(bar_1_o));  // open: RESET, LOAD, I, Carry

  // Notes on the sheet:
  //   a: 왼쪽 d: 오른쪽
  //   enter: start/pause r: score reset
  //   방어: 2점 
endmodule

module bar (
  input  [19:0] Set,
  input  RESET,
  input  LOAD,
  input  A,
  input  [4:0] I,
  input  D,
  output Carry,
  output [19:0] O
);

  wire and_1_out, and_2_out, not_1_out, not_2_out, or_1_out, pla_1_out, pla_2_out, undriven;
  wire [4:0] counter_1_q;

  not not_1 (not_1_out, pla_2_out);
  and and_1 (and_1_out, A, not_1_out);
  and and_2 (and_2_out, D, not_2_out);
  not not_2 (not_2_out, pla_1_out);
  or or_1 (or_1_out, and_1_out, and_2_out);
  Counter #(.max('he), .width(5)) counter_1 (
    .clr(RESET), .load(LOAD), .up(and_1_out), .count(undriven), .clk(or_1_out), .D(I), .carry(Carry),
    .Q(counter_1_q));
  PLA #(.in_width(5), .out_width(1), .\table ("00000 1")) pla_1 (.in(counter_1_q), .out(pla_1_out));
  PLA #(.in_width(5), .out_width(1), .\table ("01110 1")) pla_2 (.in(counter_1_q), .out(pla_2_out));
  Shifter #(.width(20)) shifter_1 (.in(Set), .\dist (counter_1_q), .out(O));
endmodule

// left/right
module ball (
  input  [19:0] Set,
  input  RESET,
  input  LOAD,
  input  Count,
  input  EN,
  input  CL,
  input  [4:0] I,
  output Carry,
  output [19:0] O
);

  wire [4:0] counter_1_q;

  Counter #(.max('h13), .ongoal("stay"), .width(5)) counter_1 (
    .clr(RESET), .load(LOAD), .up(Count), .count(EN), .clk(CL), .D(I), .carry(Carry), .Q(counter_1_q));
  Shifter #(.width(20)) shifter_1 (.in(Set), .\dist (counter_1_q), .out(O));
endmodule

module score (
  input  Reset,
  input  i,
  output [6:0] ten,
  output [6:0] hundred,
  output [6:0] one
);

  wire binary_to_bcd_converter_1_p4, binary_to_bcd_converter_1_p5, binary_to_bcd_converter_1_p6,
       counter_1_carry;
  wire [8:0] counter_1_q;

  Counter #(.max('h1ff), .width(9)) counter_1 (
    .clr(Reset), .clk(i), .carry(counter_1_carry), .Q(counter_1_q));  // open: load, up, count, D
  PLA #(.in_width(4), .out_width(7), .\table ("0000 1111110\n0001 0110000\n0010 1101101\n0011 1111001\n0100 0110011\n0101 1011011\n0110 1011111\n0111 1110000\n1000 1111111\n1001 1111011")) pla_1 (
    .in(binary_to_bcd_converter_1_p4), .out(hundred));
  // Binary_to_BCD_converter binary_to_bcd_converter_1: pin names not known; wires that end beside it: counter_1_carry, counter_1_carry, counter_1_q, binary_to_bcd_converter_1_p4, binary_to_bcd_converter_1_p5, binary_to_bcd_converter_1_p6
  PLA #(.in_width(4), .out_width(7), .\table ("0000 1111110\n0001 0110000\n0010 1101101\n0011 1111001\n0100 0110011\n0101 1011011\n0110 1011111\n0111 1110000\n1000 1111111\n1001 1111011")) pla_2 (
    .in(binary_to_bcd_converter_1_p5), .out(ten));
  PLA #(.in_width(4), .out_width(7), .\table ("0000 1111110\n0001 0110000\n0010 1101101\n0011 1111001\n0100 0110011\n0101 1011011\n0110 1011111\n0111 1110000\n1000 1111111\n1001 1111011")) pla_3 (
    .in(binary_to_bcd_converter_1_p6), .out(one));
endmodule
